// Logisim project First Homework.circ as structural Verilog: 1 circuit, main circuit main
module main (
  input  a,
  input  b,
  input  c,
  input  d,
  output x
);

  wire and_1_out, nand_1_out, nor_1_out, not_1_out, or_1_out, xor_1_out;

  not not_1 (not_1_out, b);
  and and_1 (and_1_out, b, d);
  xor xor_1 (xor_1_out, a, c);
  nor nor_1 (nor_1_out, not_1_out, and_1_out, and_1_out);
  nand nand_1 (nand_1_out, xor_1_out, not_1_out);
  or or_1 (or_1_out, nand_1_out, nor_1_out);
endmodule
