// Logisim project Logism Example XOR Circut (Question 8f).circ as structural Verilog: 1 circuit, main circuit main
module main (
  input  x,
  input  y,
  output \output 
);

  wire and_1_out, and_2_out, not_1_out, not_2_out;

  not not_1 (not_1_out, x);
  not not_2 (not_2_out, y);
  and and_1 (and_1_out, not_1_out, y, y);
  and and_2 (and_2_out, x, not_2_out);
  or or_1 (\output , and_1_out, and_2_out);

  // Notes on the sheet:
  //   XOR Circut
endmodule
