// Logisim project Question 9.circ as structural Verilog: 1 circuit, main circuit main
module main (
  input  CarryIn,
  input  InvertA,
  input  InputA,
  input  EnableA,
  input  Input_B,
  input  Enable_B,
  input  Function0,
  input  Function1,
  output Output,
  output Carryout
);

  wire A___B_out, AB_out, and_1_out, and_2_out, and_3_out, and_4_out, and_5_out, and_6_out, and_7_out,
       and_8_out, and_9_out, and_10_out, and_11_out, and_12_out, not_1_out, not_2_out, not_3_out, not_4_out,
       Not_B_out, xor_1_out, xor_2_out, xor_3_out;

  and and_1 (and_1_out, InputA, EnableA);
  and and_2 (and_2_out, Input_B, Enable_B);
  not not_1 (not_1_out, Function0);
  not not_2 (not_2_out, Function1);
  not not_3 (not_3_out, Function0);
  not not_4 (not_4_out, Function1);
  xor xor_1 (xor_1_out, InvertA, and_1_out);
  and and_3 (and_3_out, not_1_out, not_2_out);
  and and_4 (and_4_out, Function1, not_3_out);
  and and_5 (and_5_out, not_4_out, Function0);
  and and_6 (and_6_out, Function0, Function1);
  and AB (AB_out, xor_1_out, and_2_out);
  or A___B (A___B_out, xor_1_out, and_2_out);
  not Not_B (Not_B_out, and_2_out);
  and and_7 (and_7_out, AB_out, and_3_out);
  and and_8 (and_8_out, A___B_out, and_4_out);
  and and_9 (and_9_out, Not_B_out, and_5_out);
  and and_10 (and_10_out, and_6_out, xor_1_out, and_2_out);
  or or_1 (Carryout, and_10_out, and_11_out);
  xor xor_2 (xor_2_out, and_2_out, xor_1_out);
  and and_11 (and_11_out, and_6_out, CarryIn, xor_2_out);
  xor xor_3 (xor_3_out, CarryIn, xor_2_out);
  and and_12 (and_12_out, xor_3_out, and_6_out);
  or or_2 (Output, and_7_out, and_8_out, and_9_out, and_12_out);

  // Notes on the sheet:
  //   Sum
endmodule
