// Logisim project 3-bit-counter.circ as structural Verilog: 1 circuit, main circuit main
module main (
  input  in_1,
  output _0,
  output _1,
  output _2
);

  wire and_1_out, clock_1_out;

  Clock clock_1 (.out(clock_1_out));
  J_K_Flip_Flop j_k_ff_1 (.J(in_1), .clk(clock_1_out), .K(in_1), .Q(_0));  // open: Qn, preset, en, reset
  and and_1 (and_1_out, _0, _1);
  J_K_Flip_Flop j_k_ff_2 (.J(_0), .clk(clock_1_out), .K(_0), .Q(_1));  // open: Qn, preset, en, reset
  J_K_Flip_Flop j_k_ff_3 (.J(and_1_out), .clk(clock_1_out), .K(and_1_out), .Q(_2));  // open: Qn, preset, en, reset
endmodule
