// Logisim project 3 bit counter up.circ as structural Verilog: 1 circuit, main circuit main
module main (
  output out_1,
  output out_2,
  output out_3
);

  wire and_1_out, and_2_out, and_3_out, and_4_out, clock_1_out, not_1_out, not_2_out, not_3_out, or_1_out,
       or_2_out, or_3_out;

  Clock clock_1 (.out(clock_1_out));
  and and_1 (and_1_out, or_2_out, out_1);
  D_Flip_Flop A (.clk(clock_1_out), .D(or_1_out), .Q(out_1));  // open: Qn, preset, en, reset
  and and_2 (and_2_out, not_1_out, out_2);
  or or_1 (or_1_out, and_1_out, and_3_out);
  not not_1 (not_1_out, out_3);
  D_Flip_Flop B (.clk(clock_1_out), .D(or_3_out), .Q(out_3));  // open: Qn, preset, en, reset
  not not_2 (not_2_out, out_1);
  or or_2 (or_2_out, not_1_out, not_3_out);
  and and_3 (and_3_out, out_3, not_2_out, out_2);
  not not_3 (not_3_out, out_2);
  D_Flip_Flop C (.clk(clock_1_out), .D(not_3_out), .Q(out_2));  // open: Qn, preset, en, reset
  and and_4 (and_4_out, out_3, not_3_out);
  or or_3 (or_3_out, and_4_out, and_2_out);
endmodule
