// Logisim project 4 bit counter up.circ as structural Verilog: 1 circuit, main circuit main
module main (
  output out_1,
  output out_2,
  output out_3,
  output out_4
);

  wire and_1_out, and_2_out, and_3_out, and_4_out, and_5_out, and_6_out, and_7_out, and_8_out, clock_1_out,
       not_1_out, not_2_out, not_3_out, not_4_out, or_1_out, or_2_out, or_3_out, or_4_out, or_5_out, or_6_out;

  D_Flip_Flop d_ff_1 (.clk(clock_1_out), .D(or_1_out), .Q(out_1));  // open: Qn, preset, en, reset
  Clock clock_1 (.out(clock_1_out));
  or or_1 (or_1_out, and_2_out, and_7_out);
  and and_1 (and_1_out, or_3_out, out_2);
  and and_2 (and_2_out, out_1, or_4_out);
  D_Flip_Flop A (.clk(clock_1_out), .D(or_2_out), .Q(out_2));  // open: Qn, preset, en, reset
  and and_3 (and_3_out, not_1_out, out_3);
  or or_2 (or_2_out, and_1_out, and_4_out);
  not not_1 (not_1_out, out_4);
  D_Flip_Flop B (.clk(clock_1_out), .D(or_5_out), .Q(out_4));  // open: Qn, preset, en, reset
  not not_2 (not_2_out, out_2);
  or or_3 (or_3_out, not_1_out, not_3_out);
  and and_4 (and_4_out, out_4, not_2_out, out_3);
  or or_4 (or_4_out, not_1_out, not_2_out);
  not not_3 (not_3_out, out_3);
  D_Flip_Flop C (.clk(clock_1_out), .D(not_3_out), .Q(out_3));  // open: Qn, preset, en, reset
  and and_5 (and_5_out, out_1, not_3_out);
  and and_6 (and_6_out, out_4, not_3_out);
  or or_5 (or_5_out, and_6_out, and_3_out);
  or or_6 (or_6_out, and_5_out, and_8_out);
  not not_4 (not_4_out, out_1);
  and and_7 (and_7_out, or_6_out, out_4);
  and and_8 (and_8_out, out_2, not_4_out, out_3);
endmodule
