// Logisim project 3 bit storage.circ as structural Verilog: 1 circuit, main circuit main
module main (
  input  A,
  input  B,
  input  C,
  output Q1,
  output Q0,
  output Q2
);

  wire clock_1_out;

  D_Flip_Flop d_ff_1 (.clk(clock_1_out), .D(A), .Q(Q2));  // open: Qn, preset, en, reset
  Clock clock_1 (.out(clock_1_out));
  D_Flip_Flop d_ff_2 (.clk(clock_1_out), .D(B), .Q(Q1));  // open: Qn, preset, en, reset
  D_Flip_Flop d_ff_3 (.clk(clock_1_out), .D(C), .Q(Q0));  // open: Qn, preset, en, reset
endmodule
