// Logisim project number-generator.circ as structural Verilog: 1 circuit, main circuit main
module main (
  input  nReset,
  output Qa,
  output Qb,
  output Qc,
  output Qd
);

  wire clock_1_out, d_ff_1_qn, d_ff_3_qn, not_1_out, xor_1_out, xor_2_out;

  Clock clock_1 (.out(clock_1_out));
  xor xor_1 (xor_1_out, Qd, d_ff_3_qn);
  not not_1 (not_1_out, nReset);
  D_Flip_Flop d_ff_1 (.clk(clock_1_out), .D(xor_1_out), .Q(Qa), .Qn(d_ff_1_qn), .reset(not_1_out));  // open: preset, en
  D_Flip_Flop d_ff_2 (.clk(clock_1_out), .D(d_ff_1_qn), .Q(Qb), .reset(not_1_out));  // open: Qn, preset, en
  D_Flip_Flop d_ff_3 (.clk(clock_1_out), .D(Qb), .Q(Qc), .Qn(d_ff_3_qn), .reset(not_1_out));  // open: preset, en
  xor xor_2 (xor_2_out, Qa, Qc);
  D_Flip_Flop d_ff_4 (.clk(clock_1_out), .D(xor_2_out), .Q(Qd), .reset(not_1_out));  // open: Qn, preset, en

  // Notes on the sheet:
  //   Clock
endmodule
