// Logisim project Question 12 + 14.circ as structural Verilog: 1 circuit, main circuit main
module main (
  input  X,
  output A,
  output C,
  output B
);

  wire and_1_out, and_2_out, clock_1_out, not_1_out, not_2_out, not_3_out, or_1_out, or_2_out, or_3_out,
       or_4_out, or_5_out, or_6_out;

  not not_1 (not_1_out, B);
  or or_1 (or_1_out, X, not_1_out);
  or or_2 (or_2_out, B, X);
  J_K_Flip_Flop u_B (.J(or_2_out), .clk(clock_1_out), .K(or_1_out), .Q(B));  // open: Qn, preset, en, reset
  and and_1 (and_1_out, X, B);
  Clock clock_1 (.out(clock_1_out));
  and and_2 (and_2_out, and_1_out, A);
  not not_2 (not_2_out, A);
  or or_3 (or_3_out, A, and_1_out);
  or or_4 (or_4_out, and_1_out, not_2_out);
  J_K_Flip_Flop u_A (.J(or_3_out), .clk(clock_1_out), .K(or_4_out), .Q(A));  // open: Qn, preset, en, reset
  or or_5 (or_5_out, and_2_out, C);
  not not_3 (not_3_out, C);
  J_K_Flip_Flop u_C (.J(or_5_out), .clk(clock_1_out), .K(or_6_out), .Q(C));  // open: Qn, preset, en, reset
  or or_6 (or_6_out, not_3_out, and_2_out);
endmodule
