// Logisim project Question 8 Circut.circ as structural Verilog: 1 circuit, main circuit main
module main (
  input  in_1,
  input  in_2,
  output out_3,
  output out_4
);

  wire adder_1_cout, clock_1_out;

  Adder #(.width(1)) adder_1 (.a(in_1), .b(in_2), .out(out_3), .cin(out_4), .cout(adder_1_cout));
  Clock clock_1 (.out(clock_1_out));
  D_Flip_Flop d_ff_1 (.clk(clock_1_out), .D(adder_1_cout), .Q(out_4));  // open: Qn, preset, en, reset
endmodule
