// Logisim project Question 8.circ as structural Verilog: 1 circuit, main circuit main
module main (
  input  x,
  input  y,
  output S,
  output Q
);

  wire adder_1_cout, clock_1_out;

  Adder #(.width(1)) adder_1 (.a(x), .b(y), .out(S), .cin(Q), .cout(adder_1_cout));
  Clock clock_1 (.out(clock_1_out));
  D_Flip_Flop d_ff_1 (.clk(clock_1_out), .D(adder_1_cout), .Q(Q));  // open: Qn, preset, en, reset
endmodule
