// Logisim project Logisim.circ as structural Verilog: 1 circuit, main circuit main
module main (
  input  in_1,
  input  in_2,
  input  in_3
);

  wire clock_1_out;
  wire [7:0] register_1_q;

  Register register_1 (.Q(register_1_q));  // open: D, en, clk, clr
  Clock clock_1 (.out(clock_1_out));
  RAM ram_1 (.addr(register_1_q), .sel(in_2), .clk(clock_1_out), .ld(in_3), .clr(in_1));  // open: data
endmodule
